# Fritzing sketch sketch (saved by Fritzing 0.9.3b)
breadboards: 1

parts:
  Part1 = Arduino Uno (Rev3)
  Part2 = InvenSense MPU6050
  Part3 = XBee USB Mini Adapter
  Part4 = Adafruit 4-channel I2C-safe Bi-directional Logic Level Converter [part_number="Adafruit #757"]
  J1 = Basic Servo

nets:
  N1: Part1.D10_PWM/SS, J1.pulse
  N2: Part1.A4/SDA, Part4.A4
  N3: Part1.A5/SCL, Part4.A3
  N4: Part1.D0/RX, Part1.D1/TX, Part3.RXD, Part3.TXD
  N5: Part1.3V3, Part4.LV
  5V: Part1.5V, Part2.VCC, Part3.5V, Part4.HV
  GND: Part1.GND, Part2.GND, Part3.GND, Part4.GND, J1.gnd
  N6: Part2.SCL, Part4.B3
  N7: Part2.SDA, Part4.B4

custom parts:
  Adafruit 4-channel I2C-safe Bi-directional Logic Level Converter: Because the Arduino (and Basic Stamp) are 5V devices, and most modern sensors, displays, flash cards and modes are 3.3V-only, many makers find that they need to perform level shifting/conversion to protect the 3.3V device from 5V. We do have some other handy level shifters in the shop, from the DIP 74LVC245 to the fancy bi-directional TXB0108. However, neither of these are happy to work with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
